# Fritzing sketch schematic (saved by Fritzing 0.9.4)

parts:
  Composant1 = Arduino Due (Rev2b)
  M2 = ESC
  920KV_Motor2 = DJI 920 KV Motor
  Power_plug2 = Power plug  # not connected
  920KV_Motor3 = DJI 920 KV Motor
  M3 = ESC
  M4 = ESC
  920KV_Motor4 = DJI 920 KV Motor
  M5 = ESC
  920KV_Motor5 = DJI 920 KV Motor
  ANT1 = Antenna
  Power_plug3 = Power plug
  M6 = gy9250
  OLED_I2C1 = OLED 128x64 I2C Monochrome Display

nets:
  N1: Composant1.IOREF, M6.pin1
  5V: Composant1.5V, OLED_I2C1.VDD
  GND: Composant1.GND, M6.pin2, OLED_I2C1.GND
  N2: Composant1.D8_PWM, M4.DATA
  N3: Composant1.D9_PWM, M5.DATA
  N4: Composant1.SDA1, OLED_I2C1.SDA
  N5: Composant1.SCL1, OLED_I2C1.SCK
  N6: Composant1.D4_PWM/SS1, M6.pin9
  N7: Composant1.D5_PWM, ANT1.C3
  N8: Composant1.D6_PWM, M2.DATA
  N9: Composant1.D7_PWM, M3.DATA
  N10: M2.U, 920KV_Motor2.u
  N11: M2.V, 920KV_Motor2.v
  N12: M2.W, 920KV_Motor2.w
  N13: 920KV_Motor3.w, M3.W
  N14: 920KV_Motor3.v, M3.V
  N15: 920KV_Motor3.u, M3.U
  N16: M4.U, 920KV_Motor4.u
  N17: M4.V, 920KV_Motor4.v
  N18: M4.W, 920KV_Motor4.w
  N19: M5.U, 920KV_Motor5.u
  N20: M5.V, 920KV_Motor5.v
  N21: M5.W, 920KV_Motor5.w
  GND_2: ANT1.GND, Power_plug3.GND
  VCC: ANT1.VCC, Power_plug3.VCC

notes:
  11.1V 3S Battery
  Motor A
  Motor B
  Motor C
  Motor D
  5V
  Connect VIN when Arduino is not powered by microUSB

custom parts:
  DJI 920 KV Motor: DJI Brushless Outrunner 2212/920K Motor F330-550
  Antenna: Random Wire Antenna
  gy9250: MPU-9250 module (three-axis gyroscope + three-axis acceleration + three-axis magnetic field). The generic model from ebay et. al. rather than the Sparkfun version.
